# Fritzing sketch SPMAKERWEEK19_esquematico_automacao (saved by Fritzing 0.9.3b)
breadboards: 1

parts:
  Componente1 = Arduino Mega 2560 (Rev3)
  U1 = POT [package=pot_alpha_rv16af-20]
  U2 = POT [package=pot_alpha_rv16af-20]
  U3 = POT [package=pot_alpha_rv16af-20]
  U6 = RELAY [package=relay-jzc]
  U7 = RELAY [package=relay-jzc]
  U8 = RELAY [package=relay-jzc]
  U9 = RELAY [package=relay-jzc]
  U10 = RELAY [package=relay-jzc]
  U11 = RELAY [package=relay-jzc]
  U12 = RELAY [package=relay-jzc]
  U13 = RELAY [package=relay-jzc]
  Power_plug1 = Power plug
  LED1 = LED - 5mm [color="Red (633nm)" package="5 mm [THT]"]
  LED2 = LED - 5mm [color="Red (633nm)" package="5 mm [THT]"]
  LED3 = LED - 5mm [color="Red (633nm)" package="5 mm [THT]"]
  LED4 = LED - 5mm [color="Red (633nm)" package="5 mm [THT]"]
  LED5 = LED - 5mm [color="Red (633nm)" package="5 mm [THT]"]
  LED6 = LED - 5mm [color="Red (633nm)" package="5 mm [THT]"]
  LED7 = LED - 5mm [color="Red (633nm)" package="5 mm [THT]"]
  LED8 = LED - 5mm [color="Red (633nm)" package="5 mm [THT]"]

nets:
  N1: Componente1.A0, U1.S
  N2: Componente1.A1, U3.S
  N3: Componente1.A2, U2.S
  N4: Componente1.D9_PWM, U13.NC
  N5: Componente1.D8_PWM, U12.NC
  N6: Componente1.D2_PWM, U6.NC
  N7: Componente1.D3_PWM, U7.NC
  N8: Componente1.D4_PWM, U8.NC
  N9: Componente1.D5_PWM, U9.NC
  N10: Componente1.D6_PWM, U10.NC
  N11: Componente1.D7_PWM, U11.NC
  N12: Componente1.5V, U1.A, U2.A, U3.A, U6.COIL1, U7.COIL1, U8.COIL1, U9.COIL1, U10.COIL1, U11.COIL1, U12.COIL1, U13.COIL1
  N13: Componente1.GND, U1.E, U2.E, U3.E, U6.COIL2, U7.COIL2, U8.COIL2, U9.COIL2, U10.COIL2, U11.COIL2, U12.COIL2, U13.COIL2
  N14: U6.NO, LED8.cathode
  N15: U6.MAIN, U7.MAIN, U8.MAIN, U9.MAIN, U10.MAIN, U11.MAIN, U12.MAIN, U13.MAIN, Power_plug1.GND
  N16: U7.NO, LED7.cathode
  N17: U8.NO, LED6.cathode
  N18: U9.NO, LED5.cathode
  N19: U10.NO, LED4.cathode
  N20: U11.NO, LED3.cathode
  N21: U12.NO, LED2.cathode
  N22: U13.NO, LED1.cathode
  N23: Power_plug1.VCC, LED1.anode, LED2.anode, LED3.anode, LED4.anode, LED5.anode, LED6.anode, LED7.anode, LED8.anode
